# Fritzing sketch cap (saved by Fritzing 0.9.3b)
breadboards: 1

parts:
  부품2 = Arduino Uno (Rev3) - ICSP
  부품3 = Arduino Mega 2560 (Rev3)
  U1 = NodeMCU V1.0
  S1 = Pushbutton [package="[THT]"]
  S2 = H-Bridge with L298N
  M1 = DC Motor
  J1 = Piezo Speaker
  부품5 = sensor_biometrico
  S3 = Pushbutton [package="[THT]"]
  VCC2 = Battery block 9V
  BT1 = Bluetooth HC-06u [package=THT]
  Matrix_keypad2 = KEYPAD 4x4
  S4 = Pushbutton [package="[THT]"]
  S5 = Pushbutton [package="[THT]"]

nets:
  N1: 부품2.ICSP_MOSI, 부품2.D11_PWM/MOSI, 부품3.D17_PWM/RX2
  GND: 부품2.GND, 부품3.D14/TX3, 부품3.GND, U1.GND, U1.D5, U1.RST, S1.Pin_3, S1.Pin_4, S2.GND, S2.IN4, J1.pin1, 부품5.GND, S3.Pin_3, S3.Pin_4, VCC2.-, BT1.GND, S4.Pin_3, S4.Pin_4, S5.Pin_3, S5.Pin_4
  N2: 부품2.D8, S4.Pin_1, S4.Pin_2
  N3: 부품2.D10_PWM/SS, S5.Pin_1, S5.Pin_2
  N4: 부품2.D12/MISO, 부품3.D16_PWM/TX2
  N5: 부품2.D2, 부품5.TX
  N6: 부품2.D3_PWM, 부품5.RX
  5V: 부품2.5V, 부품3.5V, U1.Vin, S2.5V, S2.IN3, 부품5.VCC, VCC2.+, BT1.VCC
  N7: 부품3.D19/RX1, BT1.RXD
  N8: 부품3.D18/TX1, BT1.TXD
  N9: 부품3.D15/RX3, U1.D6
  N10: 부품3.D22, Matrix_keypad2.col1
  N11: 부품3.D24, Matrix_keypad2.col2
  N12: 부품3.D26, Matrix_keypad2.col3
  N13: 부품3.D28, Matrix_keypad2.col4
  N14: 부품3.D30, Matrix_keypad2.row1
  N15: 부품3.D31, J1.pin2
  N16: 부품3.D32, Matrix_keypad2.row2
  N17: 부품3.D34, Matrix_keypad2.row3
  N18: 부품3.D36, Matrix_keypad2.row4
  N19: 부품3.D42, S3.Pin_1, S3.Pin_2
  N20: 부품3.D44, S1.Pin_1, S1.Pin_2
  N21: 부품3.D52, S2.IN1
  N22: 부품3.D53, S2.IN2
  N23: S2.M1-01, M1.pin_2
  N24: S2.M1-02, M1.pin_1

notes:
  도어락
  비밀번호 변경
  지문삭제 / 지문등록 / 비밀번호 변경
  문열기

custom parts:
  NodeMCU V1.0: ESP8266 based NodeMCU
  H-Bridge with L298N: h-bridge
  sensor_biometrico: Adafruit Optical Fingerprint Sensor
  Bluetooth HC-06u: Bluetooth HC-06 - face up, pins down 16.5mm x 37.5mm PCB
  KEYPAD 4x4: Matrix keypad 16 buttons, 4 rows x 4 columns
